# Fritzing sketch Sketch (saved by Fritzing 0.9.3b)
breadboards: 1

parts:
  U1 = NodeMCU V1.0
  HLK-PM1 = HLK-PM01
  KF-1 = KF-301 Relay [package=THT]

nets:
  N1: U1.3V3, KF-1.power
  N2: U1.GND, HLK-PM1.-Vo, KF-1.ground
  N3: U1.D5, KF-1.signal
  N4: U1.Vin, HLK-PM1.+Vo
  N5: HLK-PM1.AC#0, KF-1.C

notes:
  AC IN
  AC OUT

custom parts:
  NodeMCU V1.0: ESP8266 based NodeMCU
  KF-301 Relay: KF-301
